# Fritzing sketch Soleil (saved by Fritzing 0.9.2b)

parts:
  Q1 = Basic FET P-Channel [package="TO220 [THT]"]
  arduino = Arduino Uno (Rev3)
  Q2 = Basic FET P-Channel [package="TO220 [THT]"]
  Q3 = Basic FET P-Channel [package="TO220 [THT]"]
  LED1 = RGB LED (com. cathode, rgb) [package="5 mm [THT]"]
  J2 = screw terminal, 4 pins
  J3 = screw terminal, 4 pins
  V1 = DC Power [voltage=12V]
  R1 = Resistor [tolerance=±5% resistance=10k package=THT]
  R2 = Resistor [tolerance=±5% resistance=10k package=THT]
  R3 = Resistor [tolerance=±5% resistance=10k package=THT]
  R4 = Rotary Potentiometer (Small) [maximum_resistance=10kΩ package=THT]
  R5 = Rotary Potentiometer (Small) [maximum_resistance=10kΩ package=THT]
  R6 = Rotary Potentiometer (Small) [maximum_resistance=10kΩ package=THT]
  R7 = Rotary Potentiometer (Small) [maximum_resistance=10kΩ package=THT]

nets:
  N1: Q1.gate, arduino.D9_PWM, R1.Pin_1
  GND: Q1.drain, arduino.GND, Q2.drain, Q3.drain, V1.V-, R1.Pin_0, R2.Pin_0, R3.Pin_0, R4.leg1, R5.leg1, R6.leg1, R7.leg1
  N2: Q1.source, J3.pin2
  N3: arduino.A0, R4.wiper
  N4: arduino.A1, R5.wiper
  N5: arduino.A2, R6.wiper
  N6: arduino.A3, R7.wiper
  N7: arduino.D10_PWM/SS, Q2.gate
  N8: arduino.D11_PWM/MOSI, Q3.gate
  N9: arduino.5V, R4.leg2, R5.leg2, R6.leg2, R7.leg2
  N10: Q2.source, J3.pin3
  N11: Q3.source, J3.pin4
  N12: LED1.red_anode, J2.pin2
  N13: LED1.common_cathode, J2.pin1
  N14: LED1.green_anode, J2.pin4
  N15: LED1.blue_anode, J2.pin3
  N16: J3.pin1, V1.V+

// code stored in the sketch: Soleil.ino
// gestion des sorties
const int ledR = 3;
const int ledG = 4;
const int ledB = 5;
// gestion des entrées
const int potR = A1;
const int potG = A2;
const int potB = A4;
const int PosSoleil = A5;
// gestion des variable global
boolean Etat = true; // true = Soleil et False = Lune
int Position_Soleil = 0;

void setup() {
  // put your setup code here, to run once:
  //Définition des sorties
  pinMode(ledR, OUTPUT);
  pinMode(ledG, OUTPUT);
  pinMode(ledB, OUTPUT);
  //Définition des entrées
  pinMode(potR, INPUT);
  pinMode(potG, INPUT);
  pinMode(potB, INPUT);
  //Gestion de la liaison série
  Serial.begin(115200);
  Serial.println("Hello");
}

void loop() {
  // put your main code here, to run repeatedly:
  // commande Rouge
  /*int ValeurR = analogRead(potR);
  int ComR = map(ValeurR, 0,1023, 0 ,255);
  Serial.print("tension Rouge : ");
  Serial.println(ComR);
  analogWrite(ledR, ComR);
// commande Vert
 int ValeurG = analogRead(potG);
 int ComG = map(ValeurG, 0,1023, 0 ,255);
 Serial.print("tension Vert : ");
  Serial.println(ComG);
 analogWrite(ledG, ComG);
// commande Blue
 int ValeurB = analogRead(potB);
 int ComB = map(ValeurB, 0,1023, 0 ,255);
 Serial.print("tension Bleu : ");
 Serial.println(ComB);
 analogWrite(ledB, ComB);*/
 PositionSoleil();
 
}

void PositionSoleil () {
// récupérer la position du soleil
  int last_Pos_Soleil = Position_Soleil;
  Position_Soleil = analogRead(PosSoleil);
  //Position_Soleil = map(Position_Soleil, 0 , 1023 , 0 ,1023);
  Serial.print("Position du soleil ");
  Serial.println(Position_Soleil);
  //Serial.print("\t");
  //Serial.print("Etat : ");
  //Serial.println(Etat);
  //Allumer en soleil
  if ( (Position_Soleil >= 0 and Position_Soleil <= 115) and last_Pos_Soleil < Position_Soleil ) {  // pour gérer juste un changement d'état en buté remplacer le dernier et par ceci and Etat == 1
      // Création du fadding entre le matin et la journée
      int Red = map ( Position_Soleil , 0 , 115 , 180, 201);
      int Green = map ( Position_Soleil , 0 , 115 , 176, 255);
      int Blue = map ( Position_Soleil , 0 , 115 , 28, 69);
      affichage_Couleur(Red,Green,Blue,"Matin");
      ComLumiere(Red, Green, Blue);
  }
  if ( (Position_Soleil > 115 and Position_Soleil <= 980) and last_Pos_Soleil < Position_Soleil ) {  // pour gérer juste un changement d'état en buté remplacer le dernier et par ceci and Etat == 1
      // Création du fadding entre la journée et le soir
      int Red = map ( Position_Soleil , 115 , 980 , 201, 186);
      int Green = map ( Position_Soleil , 115 , 980 , 255, 153);
      int Blue = map ( Position_Soleil , 115 , 980 , 69, 28);
      affichage_Couleur(Red,Green,Blue,"Journee");
      ComLumiere(Red, Green, Blue);
  }
  if ( (Position_Soleil > 980 and Position_Soleil <= 1023) and last_Pos_Soleil < Position_Soleil ) {  // pour gérer juste un changement d'état en buté remplacer le dernier et par ceci and Etat == 1
      // Création du fadding entre le soir et la lune
      int Red = map ( Position_Soleil , 980 , 1023 , 186, 0);
      int Green = map ( Position_Soleil , 980 , 1023 , 153, 0);
      int Blue = map ( Position_Soleil , 980 , 1023 ,28, 0);
      affichage_Couleur(Red,Green,Blue,"Soiree");
      ComLumiere(Red, Green, Blue);
      if (Position_Soleil == 1023) {
      Etat = false;
      }
  }
  //Allumer en Lune
  if ( (Position_Soleil <= 1023 and Position_Soleil >= 980) and last_Pos_Soleil > Position_Soleil ) {  // pour gérer juste un changement d'état en buté remplacer le dernier et par ceci and Etat == 0
      // Création du fadding entre le matin et la journée
      int Red = map ( Position_Soleil , 1023 , 980 , 140, 90);
      int Green = map ( Position_Soleil , 1023 , 980 ,220, 70);
      int Blue = map ( Position_Soleil , 1023 , 980 , 28, 115);
      affichage_Couleur(Red,Green,Blue,"Matin");
      ComLumiere(Red, Green, Blue);
  }
  if ( (Position_Soleil < 980 and Position_Soleil >= 115) and last_Pos_Soleil > Position_Soleil ) {  // pour gérer juste un changement d'état en buté remplacer le dernier et par ceci and Etat == 0
      // Création du fadding entre la journée et le soir
      int Red = map ( Position_Soleil , 980 , 115 , 90, 90);
      int Green = map ( Position_Soleil , 980 , 115 , 70, 153);
      int Blue = map ( Position_Soleil , 980 , 115 , 115, 186);
      affichage_Couleur(Red,Green,Blue,"Journee");
      ComLumiere(Red, Green, Blue);
  }
  if ( (Position_Soleil < 115 and Position_Soleil >= 0) and last_Pos_Soleil > Position_Soleil ) {  // pour gérer juste un changement d'état en buté remplacer le dernier et par ceci and Etat == 0
      // Création du fadding entre le soir et la lune
      int Red = map ( Position_Soleil , 115 , 0 , 90, 0);
      int Green = map ( Position_Soleil , 115 , 0 , 153, 0);
      int Blue = map ( Position_Soleil , 115 , 0 ,186, 0);
      affichage_Couleur(Red,Green,Blue,"Soiree");
      ComLumiere(Red, Green, Blue);
      if (Position_Soleil == 1023) {
      Etat = false;
      }
  }
  
}

void ComLumiere (int Red, int Green, int Blue) {
  analogWrite(ledR, Red);
  analogWrite(ledG, Green);
  analogWrite(ledB, Blue);
}

void affichage_Couleur (int Red, int Green, int Blue, char moment[]) {
      Serial.println(moment);
      Serial.print("Rouge : ");
      Serial.print(Red);
      Serial.print("\t");
      Serial.print("Vert : ");
      Serial.print(Green);
      Serial.print("\t");
      Serial.print("Bleu : ");
      Serial.println(Blue);
}
